// Logisim project 6502_trans.circ as structural Verilog
module Clock_Generation (
  input  _1171,
  output _1163,
  output _421,
  output _710,
  output _943
);

  wire pull_resistor_2_node, pull_resistor_8_node, transistor_3_out, transistor_5_out, transistor_6_out,
       transistor_8_out, transistor_10_out, transistor_12_out, transistor_14_out, transistor_17_out,
       transistor_20_out, transistor_28_out;

  Transistor #(.\type ("n")) transistor_1 (.in(1'b0), .out(_1171), .gate(1'b0));
  Transistor #(.\type ("n")) transistor_2 (.in(1'b0), .out(_1171), .gate(1'b0));
  Transistor #(.\type ("n")) transistor_3 (.in(1'b0), .out(transistor_3_out), .gate(_1171));
  Pull_Resistor #(.pull(1)) pull_resistor_1 (.node(transistor_3_out));
  Pull_Resistor #(.pull(1)) pull_resistor_2 (.node(pull_resistor_2_node));
  Transistor #(.\type ("n")) transistor_4 (.in(1'b0), .out(pull_resistor_2_node), .gate(_1171));
  Transistor #(.\type ("n")) transistor_5 (.in(1'b0), .out(transistor_5_out), .gate(transistor_3_out));
  Pull_Resistor #(.pull(1)) pull_resistor_3 (.node(transistor_5_out));
  Transistor #(.\type ("n")) transistor_6 (.in(1'b0), .out(transistor_6_out), .gate(transistor_3_out));
  Transistor #(.\type ("n")) transistor_7 (.in(1'b0), .out(transistor_6_out), .gate(transistor_3_out));
  Transistor #(.\type ("n")) transistor_8 (.in(1'b0), .out(transistor_8_out), .gate(transistor_5_out));
  Pull_Resistor #(.pull(1)) pull_resistor_4 (.node(transistor_8_out));
  Pull_Resistor #(.pull(1)) pull_resistor_5 (.node(transistor_6_out));
  Transistor #(.\type ("n")) transistor_9 (.in(1'b0), .out(transistor_6_out), .gate(_710));
  Transistor #(.\type ("n")) transistor_10 (.in(1'b0), .out(transistor_10_out), .gate(pull_resistor_2_node));
  Pull_Resistor #(.pull(1)) pull_resistor_6 (.node(transistor_10_out));
  Transistor #(.\type ("n")) transistor_11 (.in(1'b0), .out(transistor_10_out), .gate(pull_resistor_2_node));
  Transistor #(.\type ("n")) transistor_12 (.in(1'b0), .out(transistor_12_out), .gate(pull_resistor_2_node));
  Pull_Resistor #(.pull(1)) pull_resistor_7 (.node(transistor_12_out));
  Transistor #(.\type ("n")) transistor_13 (.in(1'b0), .out(transistor_12_out), .gate(_710));
  Transistor #(.\type ("n")) transistor_14 (.in(1'b1), .out(transistor_14_out), .gate(transistor_5_out));
  Transistor #(.\type ("n")) transistor_15 (.in(1'b0), .out(transistor_14_out), .gate(transistor_8_out));
  Transistor #(.\type ("n")) transistor_16 (.in(1'b0), .out(transistor_8_out), .gate(transistor_5_out));
  Transistor #(.\type ("n")) transistor_17 (.in(1'b1), .out(transistor_17_out), .gate(transistor_3_out));
  Transistor #(.\type ("n")) transistor_18 (.in(1'b0), .out(transistor_17_out), .gate(transistor_6_out));
  Pull_Resistor #(.pull(1)) pull_resistor_8 (.node(pull_resistor_8_node));
  Transistor #(.\type ("n")) transistor_19 (.in(1'b0), .out(pull_resistor_8_node), .gate(transistor_10_out));
  Transistor #(.\type ("n")) transistor_20 (.in(1'b1), .out(transistor_20_out), .gate(pull_resistor_2_node));
  Transistor #(.\type ("n")) transistor_21 (.in(1'b0), .out(transistor_20_out), .gate(transistor_12_out));
  Transistor #(.\type ("n")) transistor_22 (.in(1'b1), .out(_710), .gate(transistor_8_out));
  Transistor #(.\type ("n")) transistor_23 (.in(1'b0), .out(_710), .gate(transistor_14_out));
  Transistor #(.\type ("n")) transistor_24 (.in(1'b0), .out(_710), .gate(transistor_14_out));
  Transistor #(.\type ("n")) transistor_25 (.in(1'b1), .out(_943), .gate(transistor_6_out));
  Transistor #(.\type ("n")) transistor_26 (.in(1'b0), .out(_943), .gate(transistor_17_out));
  Transistor #(.\type ("n")) transistor_27 (.in(1'b0), .out(_943), .gate(transistor_17_out));
  Transistor #(.\type ("n")) transistor_28 (.in(1'b1), .out(transistor_28_out), .gate(transistor_10_out));
  Transistor #(.\type ("n")) transistor_29 (.in(1'b0), .out(transistor_28_out), .gate(pull_resistor_8_node));
  Transistor #(.\type ("n")) transistor_30 (.in(1'b1), .out(_421), .gate(transistor_12_out));
  Transistor #(.\type ("n")) transistor_31 (.in(1'b0), .out(_421), .gate(transistor_20_out));
  Transistor #(.\type ("n")) transistor_32 (.in(1'b0), .out(_421), .gate(transistor_20_out));
  Transistor #(.\type ("n")) transistor_33 (.in(1'b0), .out(_710), .gate(transistor_14_out));
  Transistor #(.\type ("n")) transistor_34 (.in(1'b0), .out(_710), .gate(transistor_14_out));
  Transistor #(.\type ("n")) transistor_35 (.in(1'b0), .out(_943), .gate(transistor_17_out));
  Transistor #(.\type ("n")) transistor_36 (.in(1'b0), .out(_943), .gate(transistor_17_out));
  Transistor #(.\type ("n")) transistor_37 (.in(1'b1), .out(_1163), .gate(pull_resistor_8_node));
  Transistor #(.\type ("n")) transistor_38 (.in(1'b0), .out(_1163), .gate(transistor_28_out));
  Transistor #(.\type ("n")) transistor_39 (.in(1'b0), .out(_421), .gate(transistor_20_out));
  Transistor #(.\type ("n")) transistor_40 (.in(1'b0), .out(_421), .gate(transistor_20_out));
  Transistor #(.\type ("n")) transistor_41 (.in(1'b0), .out(_710), .gate(transistor_14_out));
  Transistor #(.\type ("n")) transistor_42 (.in(1'b0), .out(_943), .gate(1'b0));
  Transistor #(.\type ("n")) transistor_43 (.in(1'b0), .out(_1163), .gate(transistor_28_out));
  Transistor #(.\type ("n")) transistor_44 (.in(1'b0), .out(_1163), .gate(transistor_28_out));
  Transistor #(.\type ("n")) transistor_45 (.in(1'b0), .out(_1163), .gate(transistor_28_out));
  Transistor #(.\type ("n")) transistor_46 (.in(1'b0), .out(_1163), .gate(transistor_28_out));

  // Notes on the sheet:
  //   t7
  //   t965
  //   t2120
  //   t1942
  //   358
  //   t2524
  //   t452 - t453
  //   519
  //   t311
  //   1715
  //   t1342 - t1343
  //   t2558
  //   670
  //   t2743 - t2744
  //   t1169
  //   t1168
  //   1399
  //   t1344
  //   t1709
  //   1129
  //   t1035
  //   t1999
  //   t492
  //   127
  //   t1919
  //   t2179
  //   t362
  //   1467
  //   747
  //   t1627
  //   t76
  //   135
  //   t1496 - t1500
  //   1105
  //   t3057 - t3060
  //   t481
  //   1417
  //   t3
  //   t2523
  //   t551 - t555
  //   t422 - t425
endmodule

module Databus_Tristate_Buffers (
  input  _353,
  input  _97,
  input  _746,
  input  _1634,
  input  _444,
  input  _1088,
  input  _1453,
  input  _1415,
  input  _63,
  output _1005,
  output _82,
  output _945,
  output _650,
  output _1393,
  output _175,
  output _1591,
  output _1349
);

  wire pull_resistor_2_node, pull_resistor_4_node, pull_resistor_5_node, pull_resistor_6_node,
       pull_resistor_7_node, transistor_1_out, transistor_5_out, transistor_15_out, transistor_17_out,
       transistor_20_out, transistor_23_out, transistor_26_out, transistor_29_out, transistor_32_out,
       transistor_35_out, transistor_38_out, transistor_41_out, transistor_44_out, transistor_47_out,
       transistor_50_out, transistor_53_out, transistor_56_out, transistor_59_out, transistor_62_out;

  Transistor #(.\type ("n")) transistor_1 (.in(1'b0), .out(transistor_1_out), .gate(_353));
  Pull_Resistor #(.pull(1)) pull_resistor_1 (.node(transistor_1_out));
  Transistor #(.\type ("n")) transistor_2 (.in(1'b0), .out(transistor_1_out), .gate(_97));
  Pull_Resistor #(.pull(1)) pull_resistor_2 (.node(pull_resistor_2_node));
  Transistor #(.\type ("n")) transistor_3 (.in(1'b0), .out(pull_resistor_2_node), .gate(_353));
  Transistor #(.\type ("n")) transistor_4 (.in(1'b0), .out(pull_resistor_2_node), .gate(_746));
  Transistor #(.\type ("n")) transistor_5 (.in(1'b0), .out(transistor_5_out), .gate(_1634));
  Pull_Resistor #(.pull(1)) pull_resistor_3 (.node(transistor_5_out));
  Transistor #(.\type ("n")) transistor_6 (.in(1'b0), .out(transistor_5_out), .gate(_353));
  Pull_Resistor #(.pull(1)) pull_resistor_4 (.node(pull_resistor_4_node));
  Transistor #(.\type ("n")) transistor_7 (.in(1'b0), .out(pull_resistor_4_node), .gate(_353));
  Transistor #(.\type ("n")) transistor_8 (.in(1'b0), .out(pull_resistor_4_node), .gate(_444));
  Pull_Resistor #(.pull(1)) pull_resistor_5 (.node(pull_resistor_5_node));
  Transistor #(.\type ("n")) transistor_9 (.in(1'b0), .out(pull_resistor_5_node), .gate(_1088));
  Transistor #(.\type ("n")) transistor_10 (.in(1'b0), .out(pull_resistor_5_node), .gate(_353));
  Pull_Resistor #(.pull(1)) pull_resistor_6 (.node(pull_resistor_6_node));
  Transistor #(.\type ("n")) transistor_11 (.in(1'b0), .out(pull_resistor_6_node), .gate(_1453));
  Transistor #(.\type ("n")) transistor_12 (.in(1'b0), .out(pull_resistor_6_node), .gate(_353));
  Pull_Resistor #(.pull(1)) pull_resistor_7 (.node(pull_resistor_7_node));
  Transistor #(.\type ("n")) transistor_13 (.in(1'b0), .out(pull_resistor_7_node), .gate(_1415));
  Transistor #(.\type ("n")) transistor_14 (.in(1'b0), .out(pull_resistor_7_node), .gate(_353));
  Transistor #(.\type ("n")) transistor_15 (.in(1'b0), .out(transistor_15_out), .gate(_63));
  Transistor #(.\type ("n")) transistor_16 (.in(1'b0), .out(transistor_15_out), .gate(_353));
  Pull_Resistor #(.pull(1)) pull_resistor_8 (.node(transistor_15_out));
  Transistor #(.\type ("n")) transistor_17 (.in(1'b1), .out(transistor_17_out), .gate(_97));
  Transistor #(.\type ("n")) transistor_18 (.in(1'b0), .out(transistor_17_out), .gate(_353));
  Transistor #(.\type ("n")) transistor_19 (.in(1'b0), .out(transistor_17_out), .gate(_353));
  Transistor #(.\type ("n")) transistor_20 (.in(1'b1), .out(transistor_20_out), .gate(transistor_1_out));
  Transistor #(.\type ("n")) transistor_21 (.in(1'b0), .out(transistor_20_out), .gate(_353));
  Transistor #(.\type ("n")) transistor_22 (.in(1'b0), .out(transistor_20_out), .gate(_353));
  Transistor #(.\type ("n")) transistor_23 (.in(1'b1), .out(transistor_23_out), .gate(_746));
  Transistor #(.\type ("n")) transistor_24 (.in(1'b0), .out(transistor_23_out), .gate(_353));
  Transistor #(.\type ("n")) transistor_25 (.in(1'b0), .out(transistor_23_out), .gate(_353));
  Transistor #(.\type ("n")) transistor_26 (.in(1'b1), .out(transistor_26_out), .gate(pull_resistor_2_node));
  Transistor #(.\type ("n")) transistor_27 (.in(1'b0), .out(transistor_26_out), .gate(_353));
  Transistor #(.\type ("n")) transistor_28 (.in(1'b0), .out(transistor_26_out), .gate(_353));
  Transistor #(.\type ("n")) transistor_29 (.in(1'b1), .out(transistor_29_out), .gate(_1634));
  Transistor #(.\type ("n")) transistor_30 (.in(1'b0), .out(transistor_29_out), .gate(_353));
  Transistor #(.\type ("n")) transistor_31 (.in(1'b0), .out(transistor_29_out), .gate(_353));
  Transistor #(.\type ("n")) transistor_32 (.in(1'b1), .out(transistor_32_out), .gate(transistor_5_out));
  Transistor #(.\type ("n")) transistor_33 (.in(1'b0), .out(transistor_32_out), .gate(_353));
  Transistor #(.\type ("n")) transistor_34 (.in(1'b0), .out(transistor_32_out), .gate(_353));
  Transistor #(.\type ("n")) transistor_35 (.in(1'b1), .out(transistor_35_out), .gate(_444));
  Transistor #(.\type ("n")) transistor_36 (.in(1'b0), .out(transistor_35_out), .gate(_353));
  Transistor #(.\type ("n")) transistor_37 (.in(1'b0), .out(transistor_35_out), .gate(_353));
  Transistor #(.\type ("n")) transistor_38 (.in(1'b1), .out(transistor_38_out), .gate(pull_resistor_4_node));
  Transistor #(.\type ("n")) transistor_39 (.in(1'b0), .out(transistor_38_out), .gate(_353));
  Transistor #(.\type ("n")) transistor_40 (.in(1'b0), .out(transistor_38_out), .gate(_353));
  Transistor #(.\type ("n")) transistor_41 (.in(1'b1), .out(transistor_41_out), .gate(_1088));
  Transistor #(.\type ("n")) transistor_42 (.in(1'b0), .out(transistor_41_out), .gate(_353));
  Transistor #(.\type ("n")) transistor_43 (.in(1'b0), .out(transistor_41_out), .gate(_353));
  Transistor #(.\type ("n")) transistor_44 (.in(1'b1), .out(transistor_44_out), .gate(pull_resistor_5_node));
  Transistor #(.\type ("n")) transistor_45 (.in(1'b0), .out(transistor_44_out), .gate(_353));
  Transistor #(.\type ("n")) transistor_46 (.in(1'b0), .out(transistor_44_out), .gate(_353));
  Transistor #(.\type ("n")) transistor_47 (.in(1'b1), .out(transistor_47_out), .gate(_1453));
  Transistor #(.\type ("n")) transistor_48 (.in(1'b0), .out(transistor_47_out), .gate(_353));
  Transistor #(.\type ("n")) transistor_49 (.in(1'b0), .out(transistor_47_out), .gate(_353));
  Transistor #(.\type ("n")) transistor_50 (.in(1'b1), .out(transistor_50_out), .gate(pull_resistor_6_node));
  Transistor #(.\type ("n")) transistor_51 (.in(1'b0), .out(transistor_50_out), .gate(_353));
  Transistor #(.\type ("n")) transistor_52 (.in(1'b0), .out(transistor_50_out), .gate(_353));
  Transistor #(.\type ("n")) transistor_53 (.in(1'b1), .out(transistor_53_out), .gate(_1415));
  Transistor #(.\type ("n")) transistor_54 (.in(1'b0), .out(transistor_53_out), .gate(_353));
  Transistor #(.\type ("n")) transistor_55 (.in(1'b0), .out(transistor_53_out), .gate(_353));
  Transistor #(.\type ("n")) transistor_56 (.in(1'b1), .out(transistor_56_out), .gate(pull_resistor_7_node));
  Transistor #(.\type ("n")) transistor_57 (.in(1'b0), .out(transistor_56_out), .gate(_353));
  Transistor #(.\type ("n")) transistor_58 (.in(1'b0), .out(transistor_56_out), .gate(_353));
  Transistor #(.\type ("n")) transistor_59 (.in(1'b1), .out(transistor_59_out), .gate(_63));
  Transistor #(.\type ("n")) transistor_60 (.in(1'b0), .out(transistor_59_out), .gate(_353));
  Transistor #(.\type ("n")) transistor_61 (.in(1'b0), .out(transistor_59_out), .gate(_353));
  Transistor #(.\type ("n")) transistor_62 (.in(1'b1), .out(transistor_62_out), .gate(transistor_15_out));
  Transistor #(.\type ("n")) transistor_63 (.in(1'b0), .out(transistor_62_out), .gate(_353));
  Transistor #(.\type ("n")) transistor_64 (.in(1'b0), .out(transistor_62_out), .gate(_353));
  Transistor #(.\type ("n")) transistor_65 (.in(1'b0), .out(transistor_17_out), .gate(transistor_1_out));
  Transistor #(.\type ("n")) transistor_66 (.in(1'b0), .out(transistor_20_out), .gate(_97));
  Transistor #(.\type ("n")) transistor_67 (.in(1'b0), .out(transistor_23_out), .gate(pull_resistor_2_node));
  Transistor #(.\type ("n")) transistor_68 (.in(1'b0), .out(transistor_26_out), .gate(_746));
  Transistor #(.\type ("n")) transistor_69 (.in(1'b0), .out(transistor_29_out), .gate(transistor_5_out));
  Transistor #(.\type ("n")) transistor_70 (.in(1'b0), .out(transistor_32_out), .gate(_1634));
  Transistor #(.\type ("n")) transistor_71 (.in(1'b0), .out(transistor_35_out), .gate(pull_resistor_4_node));
  Transistor #(.\type ("n")) transistor_72 (.in(1'b0), .out(transistor_38_out), .gate(_444));
  Transistor #(.\type ("n")) transistor_73 (.in(1'b0), .out(transistor_41_out), .gate(pull_resistor_5_node));
  Transistor #(.\type ("n")) transistor_74 (.in(1'b0), .out(transistor_44_out), .gate(_1088));
  Transistor #(.\type ("n")) transistor_75 (.in(1'b0), .out(transistor_47_out), .gate(pull_resistor_6_node));
  Transistor #(.\type ("n")) transistor_76 (.in(1'b0), .out(transistor_50_out), .gate(_1453));
  Transistor #(.\type ("n")) transistor_77 (.in(1'b0), .out(transistor_53_out), .gate(pull_resistor_7_node));
  Transistor #(.\type ("n")) transistor_78 (.in(1'b0), .out(transistor_56_out), .gate(_1415));
  Transistor #(.\type ("n")) transistor_79 (.in(1'b0), .out(transistor_59_out), .gate(transistor_15_out));
  Transistor #(.\type ("n")) transistor_80 (.in(1'b0), .out(transistor_62_out), .gate(_63));
  Transistor #(.\type ("n")) transistor_81 (.in(1'b1), .out(_1005), .gate(transistor_17_out));
  Transistor #(.\type ("n")) transistor_82 (.in(1'b1), .out(_1005), .gate(transistor_17_out));
  Transistor #(.\type ("n")) transistor_83 (.in(1'b0), .out(_1005), .gate(transistor_20_out));
  Transistor #(.\type ("n")) transistor_84 (.in(1'b0), .out(_1005), .gate(transistor_20_out));
  Transistor #(.\type ("n")) transistor_85 (.in(1'b1), .out(_82), .gate(transistor_23_out));
  Transistor #(.\type ("n")) transistor_86 (.in(1'b1), .out(_82), .gate(transistor_23_out));
  Transistor #(.\type ("n")) transistor_87 (.in(1'b0), .out(_82), .gate(transistor_26_out));
  Transistor #(.\type ("n")) transistor_88 (.in(1'b0), .out(_82), .gate(transistor_26_out));
  Transistor #(.\type ("n")) transistor_89 (.in(1'b1), .out(_945), .gate(transistor_29_out));
  Transistor #(.\type ("n")) transistor_90 (.in(1'b1), .out(_945), .gate(transistor_29_out));
  Transistor #(.\type ("n")) transistor_91 (.in(1'b0), .out(_945), .gate(transistor_32_out));
  Transistor #(.\type ("n")) transistor_92 (.in(1'b0), .out(_945), .gate(transistor_32_out));
  Transistor #(.\type ("n")) transistor_93 (.in(1'b1), .out(_650), .gate(transistor_35_out));
  Transistor #(.\type ("n")) transistor_94 (.in(1'b1), .out(_650), .gate(transistor_35_out));
  Transistor #(.\type ("n")) transistor_95 (.in(1'b0), .out(_650), .gate(transistor_38_out));
  Transistor #(.\type ("n")) transistor_96 (.in(1'b0), .out(_650), .gate(transistor_38_out));
  Transistor #(.\type ("n")) transistor_97 (.in(1'b1), .out(_1393), .gate(transistor_41_out));
  Transistor #(.\type ("n")) transistor_98 (.in(1'b1), .out(_1393), .gate(transistor_41_out));
  Transistor #(.\type ("n")) transistor_99 (.in(1'b0), .out(_1393), .gate(transistor_44_out));
  Transistor #(.\type ("n")) transistor_100 (.in(1'b0), .out(_1393), .gate(transistor_44_out));
  Transistor #(.\type ("n")) transistor_101 (.in(1'b1), .out(_175), .gate(transistor_47_out));
  Transistor #(.\type ("n")) transistor_102 (.in(1'b1), .out(_175), .gate(transistor_47_out));
  Transistor #(.\type ("n")) transistor_103 (.in(1'b0), .out(_175), .gate(transistor_50_out));
  Transistor #(.\type ("n")) transistor_104 (.in(1'b0), .out(_175), .gate(transistor_50_out));
  Transistor #(.\type ("n")) transistor_105 (.in(1'b1), .out(_1591), .gate(transistor_53_out));
  Transistor #(.\type ("n")) transistor_106 (.in(1'b1), .out(_1591), .gate(transistor_53_out));
  Transistor #(.\type ("n")) transistor_107 (.in(1'b0), .out(_1591), .gate(transistor_56_out));
  Transistor #(.\type ("n")) transistor_108 (.in(1'b0), .out(_1591), .gate(transistor_56_out));
  Transistor #(.\type ("n")) transistor_109 (.in(1'b1), .out(_1349), .gate(transistor_59_out));
  Transistor #(.\type ("n")) transistor_110 (.in(1'b1), .out(_1349), .gate(transistor_59_out));
  Transistor #(.\type ("n")) transistor_111 (.in(1'b0), .out(_1349), .gate(transistor_62_out));
  Transistor #(.\type ("n")) transistor_112 (.in(1'b0), .out(_1349), .gate(transistor_62_out));
  Transistor #(.\type ("n")) transistor_113 (.in(1'b0), .out(_1005), .gate(transistor_20_out));
  Transistor #(.\type ("n")) transistor_114 (.in(1'b0), .out(_1005), .gate(transistor_20_out));
  Transistor #(.\type ("n")) transistor_115 (.in(1'b0), .out(_82), .gate(transistor_26_out));
  Transistor #(.\type ("n")) transistor_116 (.in(1'b0), .out(_82), .gate(transistor_26_out));
  Transistor #(.\type ("n")) transistor_117 (.in(1'b0), .out(_945), .gate(transistor_32_out));
  Transistor #(.\type ("n")) transistor_118 (.in(1'b0), .out(_945), .gate(transistor_32_out));
  Transistor #(.\type ("n")) transistor_119 (.in(1'b0), .out(_650), .gate(transistor_38_out));
  Transistor #(.\type ("n")) transistor_120 (.in(1'b0), .out(_650), .gate(transistor_38_out));
  Transistor #(.\type ("n")) transistor_121 (.in(1'b0), .out(_1393), .gate(transistor_44_out));
  Transistor #(.\type ("n")) transistor_122 (.in(1'b0), .out(_1393), .gate(transistor_44_out));
  Transistor #(.\type ("n")) transistor_123 (.in(1'b0), .out(_175), .gate(transistor_50_out));
  Transistor #(.\type ("n")) transistor_124 (.in(1'b0), .out(_175), .gate(transistor_50_out));
  Transistor #(.\type ("n")) transistor_125 (.in(1'b0), .out(_1591), .gate(transistor_56_out));
  Transistor #(.\type ("n")) transistor_126 (.in(1'b0), .out(_1591), .gate(transistor_56_out));
  Transistor #(.\type ("n")) transistor_127 (.in(1'b0), .out(_1349), .gate(transistor_62_out));
  Transistor #(.\type ("n")) transistor_128 (.in(1'b0), .out(_1349), .gate(transistor_62_out));
  Transistor #(.\type ("n")) transistor_129 (.in(1'b0), .out(_1005), .gate(transistor_20_out));
  Transistor #(.\type ("n")) transistor_130 (.in(1'b0), .out(_1005), .gate(transistor_20_out));
  Transistor #(.\type ("n")) transistor_131 (.in(1'b0), .out(_82), .gate(transistor_26_out));
  Transistor #(.\type ("n")) transistor_132 (.in(1'b0), .out(_82), .gate(transistor_26_out));
  Transistor #(.\type ("n")) transistor_133 (.in(1'b0), .out(_945), .gate(transistor_32_out));
  Transistor #(.\type ("n")) transistor_134 (.in(1'b0), .out(_945), .gate(transistor_32_out));
  Transistor #(.\type ("n")) transistor_135 (.in(1'b0), .out(_650), .gate(transistor_38_out));
  Transistor #(.\type ("n")) transistor_136 (.in(1'b0), .out(_650), .gate(transistor_38_out));
  Transistor #(.\type ("n")) transistor_137 (.in(1'b0), .out(_1393), .gate(transistor_44_out));
  Transistor #(.\type ("n")) transistor_138 (.in(1'b0), .out(_1393), .gate(transistor_44_out));
  Transistor #(.\type ("n")) transistor_139 (.in(1'b0), .out(_175), .gate(transistor_50_out));
  Transistor #(.\type ("n")) transistor_140 (.in(1'b0), .out(_175), .gate(transistor_50_out));
  Transistor #(.\type ("n")) transistor_141 (.in(1'b0), .out(_1591), .gate(transistor_56_out));
  Transistor #(.\type ("n")) transistor_142 (.in(1'b0), .out(_1591), .gate(transistor_56_out));
  Transistor #(.\type ("n")) transistor_143 (.in(1'b0), .out(_1349), .gate(transistor_62_out));
  Transistor #(.\type ("n")) transistor_144 (.in(1'b0), .out(_1349), .gate(transistor_62_out));
  Transistor #(.\type ("n")) transistor_145 (.in(1'b0), .out(_1005), .gate(transistor_20_out));
  Transistor #(.\type ("n")) transistor_146 (.in(1'b0), .out(_1005), .gate(transistor_20_out));
  Transistor #(.\type ("n")) transistor_147 (.in(1'b0), .out(_82), .gate(transistor_26_out));
  Transistor #(.\type ("n")) transistor_148 (.in(1'b0), .out(_945), .gate(transistor_32_out));
  Transistor #(.\type ("n")) transistor_149 (.in(1'b0), .out(_945), .gate(transistor_32_out));
  Transistor #(.\type ("n")) transistor_150 (.in(1'b0), .out(_650), .gate(transistor_38_out));
  Transistor #(.\type ("n")) transistor_151 (.in(1'b0), .out(_1393), .gate(transistor_44_out));
  Transistor #(.\type ("n")) transistor_152 (.in(1'b0), .out(_1393), .gate(transistor_44_out));
  Transistor #(.\type ("n")) transistor_153 (.in(1'b0), .out(_175), .gate(transistor_50_out));
  Transistor #(.\type ("n")) transistor_154 (.in(1'b0), .out(_1591), .gate(transistor_56_out));
  Transistor #(.\type ("n")) transistor_155 (.in(1'b0), .out(_1349), .gate(transistor_62_out));
  Transistor #(.\type ("n")) transistor_156 (.in(1'b0), .out(_1005), .gate(1'b0));
  Transistor #(.\type ("n")) transistor_157 (.in(1'b0), .out(_82), .gate(1'b0));
  Transistor #(.\type ("n")) transistor_158 (.in(1'b0), .out(_945), .gate(transistor_32_out));
  Transistor #(.\type ("n")) transistor_159 (.in(1'b0), .out(_945), .gate(1'b0));
  Transistor #(.\type ("n")) transistor_160 (.in(1'b0), .out(_650), .gate(1'b0));
  Transistor #(.\type ("n")) transistor_161 (.in(1'b0), .out(_1393), .gate(transistor_44_out));
  Transistor #(.\type ("n")) transistor_162 (.in(1'b0), .out(_1393), .gate(1'b0));
  Transistor #(.\type ("n")) transistor_163 (.in(1'b0), .out(_175), .gate(1'b0));
  Transistor #(.\type ("n")) transistor_164 (.in(1'b0), .out(_1591), .gate(1'b0));
  Transistor #(.\type ("n")) transistor_165 (.in(1'b0), .out(_1349), .gate(1'b0));

  // Notes on the sheet:
  //   t1034
  //   t1971
  //   t560
  //   t1492
  //   t2206
  //   t1632
  //   t1418
  //   t1569
  //   t2651
  //   t1032 - t1033
  //   769
  //   t3035
  //   t2574 - t2575
  //   t333
  //   t1630 - t1631
  //   288
  //   t1515
  //   t50 - t51
  //   t578
  //   t1416 - t1417
  //   224
  //   t3122
  //   t1510 - t1511
  //   t1254
  //   t1567 - t1568
  //   1613
  //   t2516
  //   t1609 - t1610
  //   t3034
  //   1072
  //   t2205
  //   t1514
  //   794
  //   t1970
  //   t3121
  //   37
  //   t559
  //   t2515
  //   42
  //   643
  //   t1491
  //   147
  //   1325
  //   t1712 - t1713
  //   798
  //   t154 - t155
  //   520
  //   t1536- t1537
  //   t1679 - t1680
  //   1076
  //   t382 - t383
  //   t3473 - t3480
  //   t3410 - t3416
  //   t1887 - t1893
  //   t3037 - t3045
  //   t1088 - t1096
  //   t2083
  //   t364
  //   t1445
  //   t65
  //   t3227
  //   In visual6502 1088 is listed twice, and shown as connected back to 945.  Shown here tied back to ground for digital logic to work.
endmodule

module Data_Output_Register (
  input  _710,
  input  _1108,
  input  _991,
  input  _1473,
  input  _1302,
  input  _892,
  input  _1503,
  input  _833,
  input  _493,
  output _97,
  output _746,
  output _1634,
  output _444,
  output _1088,
  output _1453,
  output _1415,
  output _63
);

  wire pull_resistor_1_node, pull_resistor_2_node, pull_resistor_3_node, pull_resistor_4_node,
       pull_resistor_5_node, pull_resistor_6_node, pull_resistor_8_node, register_1_q, register_2_q,
       register_3_q, register_4_q, register_5_q, register_6_q, register_7_q, register_8_q, transistor_7_out,
       transistor_9_out, transistor_10_out, transistor_11_out, transistor_12_out, transistor_13_out,
       transistor_14_out, transistor_15_out, transistor_16_out;

  Pull_Resistor #(.pull(1)) pull_resistor_1 (.node(pull_resistor_1_node));
  Transistor #(.\type ("n")) transistor_1 (.in(1'b0), .out(pull_resistor_1_node), .gate(_1108));
  Pull_Resistor #(.pull(1)) pull_resistor_2 (.node(pull_resistor_2_node));
  Transistor #(.\type ("n")) transistor_2 (.in(1'b0), .out(pull_resistor_2_node), .gate(_991));
  Pull_Resistor #(.pull(1)) pull_resistor_3 (.node(pull_resistor_3_node));
  Transistor #(.\type ("n")) transistor_3 (.in(1'b0), .out(pull_resistor_3_node), .gate(_1473));
  Pull_Resistor #(.pull(1)) pull_resistor_4 (.node(pull_resistor_4_node));
  Transistor #(.\type ("n")) transistor_4 (.in(1'b0), .out(pull_resistor_4_node), .gate(_1302));
  Pull_Resistor #(.pull(1)) pull_resistor_5 (.node(pull_resistor_5_node));
  Transistor #(.\type ("n")) transistor_5 (.in(1'b0), .out(pull_resistor_5_node), .gate(_892));
  Pull_Resistor #(.pull(1)) pull_resistor_6 (.node(pull_resistor_6_node));
  Transistor #(.\type ("n")) transistor_6 (.in(1'b0), .out(pull_resistor_6_node), .gate(_1503));
  Transistor #(.\type ("n")) transistor_7 (.in(1'b0), .out(transistor_7_out), .gate(_833));
  Pull_Resistor #(.pull(1)) pull_resistor_7 (.node(transistor_7_out));
  Pull_Resistor #(.pull(1)) pull_resistor_8 (.node(pull_resistor_8_node));
  Transistor #(.\type ("n")) transistor_8 (.in(1'b0), .out(pull_resistor_8_node), .gate(_493));
  Transistor #(.\type ("n")) transistor_9 (.in(pull_resistor_1_node), .out(transistor_9_out), .gate(_710));
  Transistor #(.\type ("n")) transistor_10 (.in(pull_resistor_2_node), .out(transistor_10_out), .gate(_710));
  Transistor #(.\type ("n")) transistor_11 (.in(pull_resistor_3_node), .out(transistor_11_out), .gate(_710));
  Transistor #(.\type ("n")) transistor_12 (.in(pull_resistor_4_node), .out(transistor_12_out), .gate(_710));
  Transistor #(.\type ("n")) transistor_13 (.in(pull_resistor_5_node), .out(transistor_13_out), .gate(_710));
  Transistor #(.\type ("n")) transistor_14 (.in(pull_resistor_6_node), .out(transistor_14_out), .gate(_710));
  Transistor #(.\type ("n")) transistor_15 (.in(transistor_7_out), .out(transistor_15_out), .gate(_710));
  Transistor #(.\type ("n")) transistor_16 (.in(pull_resistor_8_node), .out(transistor_16_out), .gate(_710));
  Transistor #(.\type ("n")) transistor_17 (.in(1'b0), .out(_97), .gate(register_1_q));
  Register #(.width(1), .trigger("high")) register_1 (
    .D(transistor_9_out), .Q(register_1_q), .clk(_710));  // open: en, clr
  Transistor #(.\type ("n")) transistor_18 (.in(1'b0), .out(_746), .gate(register_2_q));
  Register #(.width(1), .trigger("high")) register_2 (
    .D(transistor_10_out), .Q(register_2_q), .clk(_710));  // open: en, clr
  Transistor #(.\type ("n")) transistor_19 (.in(1'b0), .out(_1634), .gate(register_3_q));
  Register #(.width(1), .trigger("high")) register_3 (
    .D(transistor_11_out), .Q(register_3_q), .clk(_710));  // open: en, clr
  Transistor #(.\type ("n")) transistor_20 (.in(1'b0), .out(_444), .gate(register_4_q));
  Register #(.width(1), .trigger("high")) register_4 (
    .D(transistor_12_out), .Q(register_4_q), .clk(_710));  // open: en, clr
  Transistor #(.\type ("n")) transistor_21 (.in(1'b0), .out(_1088), .gate(register_5_q));
  Register #(.width(1), .trigger("high")) register_5 (
    .D(transistor_13_out), .Q(register_5_q), .clk(_710));  // open: en, clr
  Transistor #(.\type ("n")) transistor_22 (.in(1'b0), .out(_1453), .gate(register_6_q));
  Register #(.width(1), .trigger("high")) register_6 (
    .D(transistor_14_out), .Q(register_6_q), .clk(_710));  // open: en, clr
  Transistor #(.\type ("n")) transistor_23 (.in(1'b0), .out(_1415), .gate(register_7_q));
  Register #(.width(1), .trigger("high")) register_7 (
    .D(transistor_15_out), .Q(register_7_q), .clk(_710));  // open: en, clr
  Transistor #(.\type ("n")) transistor_24 (.in(1'b0), .out(_63), .gate(register_8_q));
  Register #(.width(1), .trigger("high")) register_8 (
    .D(transistor_16_out), .Q(register_8_q), .clk(_710));  // open: en, clr
  Pull_Resistor #(.pull(1)) pull_resistor_9 (.node(_97));
  Pull_Resistor #(.pull(1)) pull_resistor_10 (.node(_746));
  Pull_Resistor #(.pull(1)) pull_resistor_11 (.node(_1634));
  Pull_Resistor #(.pull(1)) pull_resistor_12 (.node(_444));
  Pull_Resistor #(.pull(1)) pull_resistor_13 (.node(_1088));
  Pull_Resistor #(.pull(1)) pull_resistor_14 (.node(_1453));
  Pull_Resistor #(.pull(1)) pull_resistor_15 (.node(_1415));
  Pull_Resistor #(.pull(1)) pull_resistor_16 (.node(_63));

  // Notes on the sheet:
  //   1687
  //   t2892
  //   t1264
  //   222
  //   t2140
endmodule

module Predecode_Register (
  input  _943,
  input  in_2,
  input  in_3,
  input  in_4,
  input  in_5,
  input  in_6,
  input  in_7,
  input  in_8,
  input  in_9,
  output _758,
  output _361,
  output _955,
  output _894,
  output _369,
  output _829,
  output _1669,
  output _1690
);

  wire pull_resistor_1_node, pull_resistor_2_node, pull_resistor_4_node, pull_resistor_5_node,
       pull_resistor_6_node, register_1_q, register_2_q, register_3_q, register_4_q, register_5_q,
       register_6_q, register_7_q, register_8_q, transistor_3_out, transistor_7_out, transistor_8_out,
       transistor_9_out, transistor_10_out, transistor_11_out, transistor_12_out, transistor_13_out,
       transistor_14_out, transistor_15_out, transistor_16_out;

  Pull_Resistor #(.pull(1)) pull_resistor_1 (.node(pull_resistor_1_node));
  Transistor #(.\type ("n")) transistor_1 (.in(1'b0), .out(pull_resistor_1_node), .gate(in_2));
  Pull_Resistor #(.pull(1)) pull_resistor_2 (.node(pull_resistor_2_node));
  Transistor #(.\type ("n")) transistor_2 (.in(1'b0), .out(pull_resistor_2_node), .gate(in_3));
  Transistor #(.\type ("n")) transistor_3 (.in(1'b0), .out(transistor_3_out), .gate(in_4));
  Pull_Resistor #(.pull(1)) pull_resistor_3 (.node(transistor_3_out));
  Pull_Resistor #(.pull(1)) pull_resistor_4 (.node(pull_resistor_4_node));
  Transistor #(.\type ("n")) transistor_4 (.in(1'b0), .out(pull_resistor_4_node), .gate(in_5));
  Pull_Resistor #(.pull(1)) pull_resistor_5 (.node(pull_resistor_5_node));
  Transistor #(.\type ("n")) transistor_5 (.in(1'b0), .out(pull_resistor_5_node), .gate(in_6));
  Pull_Resistor #(.pull(1)) pull_resistor_6 (.node(pull_resistor_6_node));
  Transistor #(.\type ("n")) transistor_6 (.in(1'b0), .out(pull_resistor_6_node), .gate(in_7));
  Transistor #(.\type ("n")) transistor_7 (.in(1'b0), .out(transistor_7_out), .gate(in_8));
  Pull_Resistor #(.pull(1)) pull_resistor_7 (.node(transistor_7_out));
  Transistor #(.\type ("n")) transistor_8 (.in(1'b0), .out(transistor_8_out), .gate(in_9));
  Pull_Resistor #(.pull(1)) pull_resistor_8 (.node(transistor_8_out));
  Transistor #(.\type ("n")) transistor_9 (.in(pull_resistor_1_node), .out(transistor_9_out), .gate(_943));
  Transistor #(.\type ("n")) transistor_10 (.in(pull_resistor_2_node), .out(transistor_10_out), .gate(_943));
  Transistor #(.\type ("n")) transistor_11 (.in(transistor_3_out), .out(transistor_11_out), .gate(_943));
  Transistor #(.\type ("n")) transistor_12 (.in(pull_resistor_4_node), .out(transistor_12_out), .gate(_943));
  Transistor #(.\type ("n")) transistor_13 (.in(pull_resistor_5_node), .out(transistor_13_out), .gate(_943));
  Transistor #(.\type ("n")) transistor_14 (.in(pull_resistor_6_node), .out(transistor_14_out), .gate(_943));
  Transistor #(.\type ("n")) transistor_15 (.in(transistor_7_out), .out(transistor_15_out), .gate(_943));
  Transistor #(.\type ("n")) transistor_16 (.in(transistor_8_out), .out(transistor_16_out), .gate(_943));
  Transistor #(.\type ("n")) transistor_17 (.in(1'b0), .out(_758), .gate(register_1_q));
  Register #(.width(1), .trigger("high")) register_1 (
    .D(transistor_9_out), .Q(register_1_q), .clk(_943));  // open: en, clr
  Transistor #(.\type ("n")) transistor_18 (.in(1'b0), .out(_361), .gate(register_2_q));
  Register #(.width(1), .trigger("high")) register_2 (
    .D(transistor_10_out), .Q(register_2_q), .clk(_943));  // open: en, clr
  Transistor #(.\type ("n")) transistor_19 (.in(1'b0), .out(_955), .gate(register_3_q));
  Register #(.width(1), .trigger("high")) register_3 (
    .D(transistor_11_out), .Q(register_3_q), .clk(_943));  // open: en, clr
  Transistor #(.\type ("n")) transistor_20 (.in(1'b0), .out(_894), .gate(register_4_q));
  Register #(.width(1), .trigger("high")) register_4 (
    .D(transistor_12_out), .Q(register_4_q), .clk(_943));  // open: en, clr
  Transistor #(.\type ("n")) transistor_21 (.in(1'b0), .out(_369), .gate(register_5_q));
  Register #(.width(1), .trigger("high")) register_5 (
    .D(transistor_13_out), .Q(register_5_q), .clk(_943));  // open: en, clr
  Transistor #(.\type ("n")) transistor_22 (.in(1'b0), .out(_829), .gate(register_6_q));
  Register #(.width(1), .trigger("high")) register_6 (
    .D(transistor_14_out), .Q(register_6_q), .clk(_943));  // open: en, clr
  Transistor #(.\type ("n")) transistor_23 (.in(1'b0), .out(_1669), .gate(register_7_q));
  Register #(.width(1), .trigger("high")) register_7 (
    .D(transistor_15_out), .Q(register_7_q), .clk(_943));  // open: en, clr
  Transistor #(.\type ("n")) transistor_24 (.in(1'b0), .out(_1690), .gate(register_8_q));
  Register #(.width(1), .trigger("high")) register_8 (
    .D(transistor_16_out), .Q(register_8_q), .clk(_943));  // open: en, clr
  Pull_Resistor #(.pull(1)) pull_resistor_9 (.node(_758));
  Pull_Resistor #(.pull(1)) pull_resistor_10 (.node(_361));
  Pull_Resistor #(.pull(1)) pull_resistor_11 (.node(_955));
  Pull_Resistor #(.pull(1)) pull_resistor_12 (.node(_894));
  Pull_Resistor #(.pull(1)) pull_resistor_13 (.node(_369));
  Pull_Resistor #(.pull(1)) pull_resistor_14 (.node(_829));
  Pull_Resistor #(.pull(1)) pull_resistor_15 (.node(_1669));
  Pull_Resistor #(.pull(1)) pull_resistor_16 (.node(_1690));
endmodule

module Input_Data_Latch (
  input  _943,
  input  in_2,
  input  in_3,
  input  in_4,
  input  in_5,
  input  in_6,
  input  in_7,
  input  in_8,
  input  in_9,
  input  in_10,
  input  in_11,
  input  in_12
);

  wire pull_resistor_4_node, pull_resistor_6_node, pull_resistor_8_node, register_1_q, register_2_q,
       register_3_q, register_4_q, register_5_q, register_6_q, register_7_q, register_8_q, transistor_1_out,
       transistor_2_out, transistor_3_out, transistor_5_out, transistor_7_out, transistor_9_out,
       transistor_10_out, transistor_11_out, transistor_12_out, transistor_13_out, transistor_14_out,
       transistor_15_out, transistor_16_out, transistor_17_out, transistor_18_out, transistor_19_out,
       transistor_20_out, transistor_21_out, transistor_22_out, transistor_23_out, transistor_24_out,
       transistor_25_out, transistor_26_out, transistor_27_out, transistor_28_out, transistor_29_out,
       transistor_30_out, transistor_31_out, transistor_32_out, transistor_33_out, transistor_34_out,
       transistor_35_out, transistor_36_out, transistor_37_out, transistor_38_out, transistor_39_out,
       transistor_40_out, transistor_41_out, transistor_42_out, transistor_43_out, transistor_44_out,
       transistor_45_out, transistor_46_out, transistor_47_out, transistor_48_out;

  Transistor #(.\type ("n")) transistor_1 (.in(1'b0), .out(transistor_1_out), .gate(in_2));
  Pull_Resistor #(.pull(1)) pull_resistor_1 (.node(transistor_1_out));
  Transistor #(.\type ("n")) transistor_2 (.in(1'b0), .out(transistor_2_out), .gate(in_3));
  Pull_Resistor #(.pull(1)) pull_resistor_2 (.node(transistor_2_out));
  Transistor #(.\type ("n")) transistor_3 (.in(1'b0), .out(transistor_3_out), .gate(in_4));
  Pull_Resistor #(.pull(1)) pull_resistor_3 (.node(transistor_3_out));
  Pull_Resistor #(.pull(1)) pull_resistor_4 (.node(pull_resistor_4_node));
  Transistor #(.\type ("n")) transistor_4 (.in(1'b0), .out(pull_resistor_4_node), .gate(in_5));
  Transistor #(.\type ("n")) transistor_5 (.in(1'b0), .out(transistor_5_out), .gate(in_6));
  Pull_Resistor #(.pull(1)) pull_resistor_5 (.node(transistor_5_out));
  Pull_Resistor #(.pull(1)) pull_resistor_6 (.node(pull_resistor_6_node));
  Transistor #(.\type ("n")) transistor_6 (.in(1'b0), .out(pull_resistor_6_node), .gate(in_7));
  Transistor #(.\type ("n")) transistor_7 (.in(1'b0), .out(transistor_7_out), .gate(in_8));
  Pull_Resistor #(.pull(1)) pull_resistor_7 (.node(transistor_7_out));
  Pull_Resistor #(.pull(1)) pull_resistor_8 (.node(pull_resistor_8_node));
  Transistor #(.\type ("n")) transistor_8 (.in(1'b0), .out(pull_resistor_8_node), .gate(in_9));
  Transistor #(.\type ("n")) transistor_9 (.in(transistor_1_out), .out(transistor_9_out), .gate(_943));
  Transistor #(.\type ("n")) transistor_10 (.in(transistor_2_out), .out(transistor_10_out), .gate(_943));
  Transistor #(.\type ("n")) transistor_11 (.in(transistor_3_out), .out(transistor_11_out), .gate(_943));
  Transistor #(.\type ("n")) transistor_12 (.in(pull_resistor_4_node), .out(transistor_12_out), .gate(_943));
  Transistor #(.\type ("n")) transistor_13 (.in(transistor_5_out), .out(transistor_13_out), .gate(_943));
  Transistor #(.\type ("n")) transistor_14 (.in(pull_resistor_6_node), .out(transistor_14_out), .gate(_943));
  Transistor #(.\type ("n")) transistor_15 (.in(transistor_7_out), .out(transistor_15_out), .gate(_943));
  Transistor #(.\type ("n")) transistor_16 (.in(pull_resistor_8_node), .out(transistor_16_out), .gate(_943));
  Transistor #(.\type ("n")) transistor_17 (.in(1'b0), .out(transistor_17_out), .gate(register_1_q));
  Register #(.width(1), .trigger("high")) register_1 (
    .D(transistor_9_out), .Q(register_1_q), .clk(_943));  // open: en, clr
  Transistor #(.\type ("n")) transistor_18 (.in(1'b0), .out(transistor_18_out), .gate(register_2_q));
  Register #(.width(1), .trigger("high")) register_2 (
    .D(transistor_10_out), .Q(register_2_q), .clk(_943));  // open: en, clr
  Transistor #(.\type ("n")) transistor_19 (.in(1'b0), .out(transistor_19_out), .gate(register_3_q));
  Register #(.width(1), .trigger("high")) register_3 (
    .D(transistor_11_out), .Q(register_3_q), .clk(_943));  // open: en, clr
  Transistor #(.\type ("n")) transistor_20 (.in(1'b0), .out(transistor_20_out), .gate(register_4_q));
  Register #(.width(1), .trigger("high")) register_4 (
    .D(transistor_12_out), .Q(register_4_q), .clk(_943));  // open: en, clr
  Transistor #(.\type ("n")) transistor_21 (.in(1'b0), .out(transistor_21_out), .gate(register_5_q));
  Register #(.width(1), .trigger("high")) register_5 (
    .D(transistor_13_out), .Q(register_5_q), .clk(_943));  // open: en, clr
  Transistor #(.\type ("n")) transistor_22 (.in(1'b0), .out(transistor_22_out), .gate(register_6_q));
  Register #(.width(1), .trigger("high")) register_6 (
    .D(transistor_14_out), .Q(register_6_q), .clk(_943));  // open: en, clr
  Transistor #(.\type ("n")) transistor_23 (.in(1'b0), .out(transistor_23_out), .gate(register_7_q));
  Register #(.width(1), .trigger("high")) register_7 (
    .D(transistor_15_out), .Q(register_7_q), .clk(_943));  // open: en, clr
  Transistor #(.\type ("n")) transistor_24 (.in(1'b0), .out(transistor_24_out), .gate(register_8_q));
  Register #(.width(1), .trigger("high")) register_8 (
    .D(transistor_16_out), .Q(register_8_q), .clk(_943));  // open: en, clr
  Pull_Resistor #(.pull(1)) pull_resistor_9 (.node(transistor_17_out));
  Transistor #(.\type ("n")) transistor_25 (.in(transistor_17_out), .out(transistor_25_out), .gate(in_10));
  Pull_Resistor #(.pull(1)) pull_resistor_10 (.node(transistor_18_out));
  Transistor #(.\type ("n")) transistor_26 (.in(transistor_18_out), .out(transistor_26_out), .gate(in_10));
  Pull_Resistor #(.pull(1)) pull_resistor_11 (.node(transistor_19_out));
  Transistor #(.\type ("n")) transistor_27 (.in(transistor_19_out), .out(transistor_27_out), .gate(in_10));
  Pull_Resistor #(.pull(1)) pull_resistor_12 (.node(transistor_20_out));
  Transistor #(.\type ("n")) transistor_28 (.in(transistor_20_out), .out(transistor_28_out), .gate(in_10));
  Pull_Resistor #(.pull(1)) pull_resistor_13 (.node(transistor_21_out));
  Transistor #(.\type ("n")) transistor_29 (.in(transistor_21_out), .out(transistor_29_out), .gate(in_10));
  Pull_Resistor #(.pull(1)) pull_resistor_14 (.node(transistor_22_out));
  Transistor #(.\type ("n")) transistor_30 (.in(transistor_22_out), .out(transistor_30_out), .gate(in_10));
  Pull_Resistor #(.pull(1)) pull_resistor_15 (.node(transistor_23_out));
  Transistor #(.\type ("n")) transistor_31 (.in(transistor_23_out), .out(transistor_31_out), .gate(in_10));
  Pull_Resistor #(.pull(1)) pull_resistor_16 (.node(transistor_24_out));
  Transistor #(.\type ("n")) transistor_32 (.in(transistor_24_out), .out(transistor_32_out), .gate(in_10));
  Transistor #(.\type ("n")) transistor_33 (.in(transistor_17_out), .out(transistor_33_out), .gate(in_11));
  Transistor #(.\type ("n")) transistor_34 (.in(transistor_18_out), .out(transistor_34_out), .gate(in_11));
  Transistor #(.\type ("n")) transistor_35 (.in(transistor_19_out), .out(transistor_35_out), .gate(in_11));
  Transistor #(.\type ("n")) transistor_36 (.in(transistor_20_out), .out(transistor_36_out), .gate(in_11));
  Transistor #(.\type ("n")) transistor_37 (.in(transistor_21_out), .out(transistor_37_out), .gate(in_11));
  Transistor #(.\type ("n")) transistor_38 (.in(transistor_22_out), .out(transistor_38_out), .gate(in_11));
  Transistor #(.\type ("n")) transistor_39 (.in(transistor_23_out), .out(transistor_39_out), .gate(in_11));
  Transistor #(.\type ("n")) transistor_40 (.in(transistor_24_out), .out(transistor_40_out), .gate(in_11));
  Transistor #(.\type ("n")) transistor_41 (.in(transistor_17_out), .out(transistor_41_out), .gate(in_12));
  Transistor #(.\type ("n")) transistor_42 (.in(transistor_18_out), .out(transistor_42_out), .gate(in_12));
  Transistor #(.\type ("n")) transistor_43 (.in(transistor_19_out), .out(transistor_43_out), .gate(in_12));
  Transistor #(.\type ("n")) transistor_44 (.in(transistor_20_out), .out(transistor_44_out), .gate(in_12));
  Transistor #(.\type ("n")) transistor_45 (.in(transistor_21_out), .out(transistor_45_out), .gate(in_12));
  Transistor #(.\type ("n")) transistor_46 (.in(transistor_22_out), .out(transistor_46_out), .gate(in_12));
  Transistor #(.\type ("n")) transistor_47 (.in(transistor_23_out), .out(transistor_47_out), .gate(in_12));
  Transistor #(.\type ("n")) transistor_48 (.in(transistor_24_out), .out(transistor_48_out), .gate(in_12));
endmodule

module Databus_Precharge_Mosfets (
  input  _943,
  output out_2,
  output out_3,
  output out_4,
  output out_5,
  output out_6,
  output out_7,
  output out_8,
  output out_9
);

  Transistor #(.\type ("n")) transistor_1 (.in(1'b1), .out(out_2), .gate(_943));
  Transistor #(.\type ("n")) transistor_2 (.in(1'b1), .out(out_3), .gate(_943));
  Transistor #(.\type ("n")) transistor_3 (.in(1'b1), .out(out_4), .gate(_943));
  Transistor #(.\type ("n")) transistor_4 (.in(1'b1), .out(out_5), .gate(_943));
  Transistor #(.\type ("n")) transistor_5 (.in(1'b1), .out(out_6), .gate(_943));
  Transistor #(.\type ("n")) transistor_6 (.in(1'b1), .out(out_7), .gate(_943));
  Transistor #(.\type ("n")) transistor_7 (.in(1'b1), .out(out_8), .gate(_943));
  Transistor #(.\type ("n")) transistor_8 (.in(1'b1), .out(out_9), .gate(_943));
endmodule
